# Fritzing sketch Esquema_1Trabalho (saved by Fritzing 0.9.3b)
breadboards: 1

parts:
  Part1 = Arduino Mega 2560 (Rev3)
  R1 = Resistor [tolerance=±5% resistance=1k package=THT]
  R2 = Resistor [tolerance=±5% resistance=1k package=THT]
  R3 = Resistor [tolerance=±5% resistance=1k package=THT]
  R4 = Resistor [tolerance=±5% resistance=1k package=THT]
  R5 = Resistor [tolerance=±5% resistance=1k package=THT]
  R6 = Resistor [tolerance=±5% resistance=1k package=THT]
  R7 = Resistor [tolerance=±5% resistance=1k package=THT]
  R8 = Resistor [tolerance=±5% resistance=1k package=THT]
  R9 = Resistor [tolerance=±5% resistance=1k package=THT]
  R10 = Resistor [tolerance=±5% resistance=1k package=THT]
  R11 = Resistor [tolerance=±5% resistance=1k package=THT]
  R12 = Resistor [tolerance=±5% resistance=1k package=THT]
  R13 = Resistor [tolerance=±5% resistance=1k package=THT]
  R14 = Resistor [tolerance=±5% resistance=1k package=THT]
  R15 = Resistor [tolerance=±5% resistance=1k package=THT]
  R16 = Resistor [tolerance=±5% resistance=1k package=THT]
  R17 = Resistor [tolerance=±5% resistance=1k package=THT]
  R18 = Resistor [tolerance=±5% resistance=1k package=THT]
  R19 = Resistor [tolerance=±5% resistance=1k package=THT]

nets:
  N1: Part1.GND, R1.Pin_0
  N2: Part1.D22, R5.Pin_1
  N3: Part1.D23, R15.Pin_1
  N4: Part1.D24, R16.Pin_1
  N5: Part1.D25, R17.Pin_1
  N6: Part1.D26, R18.Pin_1
  N7: Part1.D27, R19.Pin_1
  N8: R1.Pin_1, R2.Pin_0
  N9: R2.Pin_1, R3.Pin_0, R4.Pin_0
  N10: R3.Pin_1, R5.Pin_0
  N11: R4.Pin_1, R6.Pin_0, R11.Pin_0
  N12: R6.Pin_1, R15.Pin_0
  N13: R7.Pin_0, R11.Pin_1, R12.Pin_0
  N14: R7.Pin_1, R16.Pin_0
  N15: R8.Pin_0, R12.Pin_1, R13.Pin_0
  N16: R8.Pin_1, R17.Pin_0
  N17: R9.Pin_0, R13.Pin_1, R14.Pin_0
  N18: R9.Pin_1, R18.Pin_0
  N19: R10.Pin_0, R14.Pin_1
  N20: R10.Pin_1, R19.Pin_0
